# Fritzing sketch ArduinoFocuser (saved by Fritzing 0.9.3b)
circuit board: 10.8886cm x 8.71104cm
breadboards: 1

parts:
  Arduino_Nano = Arduino Nano (Rev3.0) (ICSP)
  EasyDriver = EasyDriver_v44
  J1 = Camdenboss CTB0158-4 [part_number=CTB0158-4 package=THT]
  M1 = Stepper Motor - Bipolar
  Power_plug1 = Power plug
  C1 = Capacitor Polarized [package=panasonic_d]
  LED1 = LEDs [package=led10mm]
  R1 = Resistor [tolerance=±5% resistance=220 package=THT]
  S1 = Toggle Switch [package=THT]

nets:
  N1: Arduino_Nano.RESET, C1.-
  N2: Arduino_Nano.GND, LED1.A
  N3: Arduino_Nano.D7, EasyDriver.STEP
  N4: Arduino_Nano.D8, EasyDriver.DIR
  N5: Arduino_Nano.D9, EasyDriver.ENABLE
  N6: Arduino_Nano.D12/MISO, R1.Pin_0
  N7: Arduino_Nano.5V, S1.L2
  GND: EasyDriver.GND, Power_plug1.GND
  N8: EasyDriver.V+, Power_plug1.VCC
  N9: EasyDriver.OUT2A, J1.pin2
  N10: EasyDriver.OUT2B, J1.pin1
  N11: EasyDriver.OUT1A, J1.pin4
  N12: EasyDriver.OUT1B, J1.pin3
  N13: J1.terminal_1, M1.D
  N14: J1.terminal_2, M1.B
  N15: J1.terminal_3, M1.C
  N16: J1.terminal_4, M1.A
  N17: C1.+, S1.L1
  N18: LED1.C, R1.Pin_1

notes:
  NEMA17 Unipolar stepper
  Black A
  Green A/
  Red B
  Blue B/
  12V, .5A Power Supply
  The capacitor is mandatory for ASCOM to work - the moonlite focuser isn't seen otherwise
